// Logisim project choi_yeonjoon.circ as structural Verilog: 8 circuits, main circuit main
module main (
);

  wire and_1_out, BRANCH, CLK, CLR, comparator_1_eq, comparator_2_eq, comparator_3_eq, comparator_4_lt,
       comparator_5_gt, comparator_6_gt, comparator_7_eq, comparator_8_eq, comparator_9_eq, comparator_10_eq,
       comparator_12_lt, EN, JALR, NoOp, or_2_out, STALL, WB;
  wire [0:0] comparator_6_eq;
  wire [1:0] PC_SELECT;
  wire [1:1] comparator_14_eq;
  wire [3:0] idrr_ex_buffer_1_opcode_out, idrr_ex_buffer_1_rx_in_2, idrr_ex_buffer_1_ry_in_2, OPCODE,
       OPCODE_EX, OPCODE_MEM, OPCODE_WB, REG_WB, REGNO2, Rx, Rx_EX, Rx_MEM, Rx_WB, Ry, Ry_EX, Ry_MEM, Ry_WB,
       Rz;
  wire [15:0] Unused;
  wire [23:0] bit_extender_1_out, bit_extender_3_out;
  wire [31:0] adder_2_out, FOUT1, FOUT2, idrr_ex_buffer_1_offset_out, idrr_ex_buffer_1_pc_out,
       idrr_ex_buffer_1_rdata1out, idrr_ex_buffer_1_rdata2out, mem_wb_buffer_1_ram_out_2, multiplexer_2_out,
       multiplexer_6_out, Offset, Offset_EX, Offset_MEM, OUT1, OUT2, PC_1, PC_1_EX, PC_1_IF, PC_1_MEM,
       PC_1_OFFSET, PC_1_WB, PC_q, RAM_MEM, Rdata1_EX, Rdata1_MEM, Rdata2_EX, Rdata2_MEM, RESULT, RESULT_MEM,
       RESULT_WB, rom_1_data, WB_Data;

  Multiplexer #(.enable("false")) multiplexer_1 (.in0(1'b1), .in1(1'b0), .out(EN), .sel(STALL));
  Clock Clock (.out(CLK));
  Multiplexer #(.select(2), .width(32), .enable("false")) multiplexer_2 (
    .in0(PC_1), .in1(PC_1_OFFSET), .in2(Rdata2_MEM), .in3(PC_q), .out(multiplexer_2_out), .sel(PC_SELECT));
  Register #(.width(32)) PC (.D(multiplexer_2_out), .en(EN), .Q(PC_q), .clk(CLK));  // open: clr
  or or_1 (CLR, PC_SELECT[0], PC_SELECT[1]);
  Bit_Extender #(.in_width(32), .out_width(24), .\type ("sign")) bit_extender_1 (.in(PC_q), .out(bit_extender_1_out));
  Adder #(.width(32)) adder_1 (.a(PC_q), .b(32'h1), .out(PC_1));  // open: cin, cout
  ROM #(.addrWidth(24), .dataWidth(32)) rom_1 (.addr(bit_extender_1_out), .data(rom_1_data), .sel(EN));
  IF_IDRR_Buffer if_idrr_buffer_1 (
    .PC_1(PC_1), .Instruction(rom_1_data), .Clear(CLR), .EN(EN), .Clock(CLK),
    .INST_OUT({OPCODE, Rx, Ry, Unused, Rz}), .PC_1_OUT(PC_1_IF));
  Comparator #(.width(4)) comparator_1 (.a(OPCODE_EX), .b(4'b0011), .eq(comparator_1_eq));  // open: gt, lt
  Comparator #(.width(4)) comparator_2 (.a(Rx_EX), .b(Ry), .eq(comparator_2_eq));  // open: gt, lt
  Comparator #(.width(4)) comparator_3 (.a(Rx_EX), .b(Rz), .eq(comparator_3_eq));  // open: gt, lt
  Comparator #(.width(4)) comparator_4 (.a(OPCODE), .b(4'b0010), .lt(comparator_4_lt));  // open: gt, eq
  and and_1 (and_1_out, comparator_3_eq, comparator_4_lt);
  assign Offset = {{12{Unused[15]}}, {Unused, Rz}};  // Bit_Extender bit_extender_2
  Multiplexer #(.width(4), .enable("false")) multiplexer_3 (.in0(Rz), .in1(Rx), .out(REGNO2), .sel(comparator_5_gt));
  Comparator #(.width(4)) comparator_5 (.a(OPCODE), .b(4'b0010), .gt(comparator_5_gt));  // open: eq, lt
  or or_2 (or_2_out, comparator_2_eq, and_1_out);
  and and_2 (STALL, comparator_1_eq, or_2_out);
  Dual_Ported_Register_File dual_ported_register_file_1 (
    .CLK(CLK), .WrREGNO(REG_WB), .RdREGNO1(Ry), .RdREGNO2(REGNO2), .INPUT(WB_Data), .OUT1(OUT1), .OUT2(OUT2),
    .WrEN(WB));
  IDRR_EX_Buffer idrr_ex_buffer_1 (
    .Clear(CLR), .EN(EN), .Clock(CLK), .Offset_IN(Offset), .Rdata1IN(FOUT1), .Rdata2IN(FOUT2),
    .OPCODE_IN(OPCODE), .Rx_In(Rx), .Offset_OUT(idrr_ex_buffer_1_offset_out),
    .PC_OUT(idrr_ex_buffer_1_pc_out), .Rdata1OUT(idrr_ex_buffer_1_rdata1out),
    .Rdata2OUT(idrr_ex_buffer_1_rdata2out), .OPCODE_OUT(idrr_ex_buffer_1_opcode_out),
    .Rx_IN_2(idrr_ex_buffer_1_rx_in_2), .PC_IN(PC_1_IF), .Ry_IN_2(idrr_ex_buffer_1_ry_in_2), .Ry_In(Ry));
  Register #(.width(1)) register_1 (.D(STALL), .Q(NoOp), .clk(CLK));  // open: en, clr
  Multiplexer #(.width(4), .enable("false")) multiplexer_4 (
    .in0(idrr_ex_buffer_1_rx_in_2), .in1(4'b0000), .out(Rx_EX), .sel(NoOp));
  Multiplexer #(.width(4), .enable("false")) multiplexer_5 (
    .in0(idrr_ex_buffer_1_ry_in_2), .in1(4'b0000), .out(Ry_EX), .sel(NoOp));
  Multiplexer #(.width(32), .enable("false")) multiplexer_6 (
    .in0(Rdata2_EX), .in1(Offset_EX), .out(multiplexer_6_out), .sel(comparator_6_gt));
  Multiplexer #(.width(32), .enable("false")) multiplexer_7 (
    .in0(idrr_ex_buffer_1_offset_out), .in1({32{1'b0}}), .out(Offset_EX), .sel(NoOp));
  Multiplexer #(.width(4), .enable("false")) multiplexer_8 (
    .in0(idrr_ex_buffer_1_opcode_out), .in1(4'b0000), .out(OPCODE_EX), .sel(NoOp));
  Comparator #(.width(4)) comparator_6 (
    .a(OPCODE_EX), .b(4'b0001), .gt(comparator_6_gt), .eq(comparator_6_eq[0]));  // open: lt
  ALU alu_1 (.FUNC({1'b0, comparator_6_eq[0]}), .A(Rdata1_EX), .B(multiplexer_6_out), .OUT(RESULT));
  Forwarding_Unit forwarding_unit_1 (
    .EX_Rx(Rx_EX), .MEM_Rx(Rx_MEM), .WB_Rx(Rx_WB), .EX_Result(RESULT), .MEM_Result(RESULT_MEM),
    .RAM_Result(RAM_MEM), .WB_Result(WB_Data), .WB_OPCODE(OPCODE_WB), .EX_OPCODE(OPCODE_EX),
    .MEM_OPCODE(OPCODE_MEM), .IDDR_Rout1(OUT1), .IDDR_Rout2(OUT2), .IDDR_Ry(Ry), .IDDR_Rz(REGNO2),
    .IDDR_Opcode(OPCODE), .out_17(FOUT1), .out_18(FOUT2));  // open: IDDR_Rx
  Multiplexer #(.width(32), .enable("false")) multiplexer_9 (
    .in0(idrr_ex_buffer_1_rdata1out), .in1({32{1'b0}}), .out(Rdata1_EX), .sel(NoOp));
  Multiplexer #(.width(32), .enable("false")) multiplexer_10 (
    .in0(idrr_ex_buffer_1_pc_out), .in1({32{1'b0}}), .out(PC_1_EX), .sel(NoOp));
  Multiplexer #(.width(32), .enable("false")) multiplexer_11 (
    .in0(idrr_ex_buffer_1_rdata2out), .in1({32{1'b0}}), .out(Rdata2_EX), .sel(NoOp));
  Adder #(.width(32)) adder_2 (.a(PC_1_EX), .b(Offset_EX), .out(adder_2_out));  // open: cin, cout
  Comparator #(.width(32)) comparator_7 (.a(Rdata1_EX), .b(Rdata2_EX), .eq(comparator_7_eq));  // open: gt, lt
  EX_MEM_Buffer ex_mem_buffer_1 (
    .EN(1'b1), .Clock(CLK), .Offset_IN(Offset_EX), .Rdata1IN(Rdata1_EX), .Rdata2IN(Rdata2_EX),
    .Result_IN(RESULT), .OPCODE_IN(OPCODE_EX), .Rx_In(Rx_EX), .Ry_In(Ry_EX), .Offset_OUT(Offset_MEM),
    .Rdata1_OUT(Rdata1_MEM), .Rdata2_OUT(Rdata2_MEM), .Result_Out(RESULT_MEM), .OPCODE_OUT(OPCODE_MEM),
    .Rx_OUT(Rx_MEM), .Ry_OUT(Ry_MEM), .PC_1_IN(PC_1_EX), .PC_1_OUT(PC_1_MEM), .BRANCH(comparator_7_eq),
    .BRANCH_2(BRANCH), .NEWPC(adder_2_out), .NEWPC_2(PC_1_OFFSET));  // open: Clear
  Bit_Extender #(.in_width(32), .out_width(24)) bit_extender_3 (.in(RESULT_MEM), .out(bit_extender_3_out));
  Comparator #(.width(4)) comparator_8 (.a(4'b0100), .b(OPCODE_MEM), .eq(comparator_8_eq));  // open: gt, lt
  Comparator #(.width(4)) comparator_9 (.a(4'b0011), .b(OPCODE_MEM), .eq(comparator_9_eq));  // open: gt, lt
  Comparator #(.width(4)) comparator_10 (.a(4'b0101), .b(OPCODE_MEM), .eq(comparator_10_eq));  // open: gt, lt
  Comparator #(.width(4)) comparator_11 (.a(4'b0110), .b(OPCODE_MEM), .eq(PC_SELECT[1]));  // open: gt, lt
  and and_3 (PC_SELECT[0], BRANCH, comparator_10_eq);
  RAM #(.addrWidth(24), .dataWidth(32), .bus("separate")) ram_1 (
    .addr(bit_extender_3_out), .din(Rdata2_MEM), .data(RAM_MEM), .str(comparator_8_eq), .clk(CLK),
    .ld(comparator_9_eq));  // open: sel, clr
  MEM_WB_Buffer mem_wb_buffer_1 (
    .EN(1'b1), .Clock(CLK), .Result_IN(RESULT_MEM), .RAM_OUT(RAM_MEM), .OPCODE_IN(OPCODE_MEM),
    .Rx_In(Rx_MEM), .Ry_In(Ry_MEM), .Result_Out(RESULT_WB), .RAM_OUT_2(mem_wb_buffer_1_ram_out_2),
    .Ry_OUT(Ry_WB), .Rx_OUT(Rx_WB), .OPCODE_OUT(OPCODE_WB), .PC_1_IN(PC_1_MEM), .PC_1_OUT(PC_1_WB));
  Comparator #(.width(4)) comparator_12 (.a(OPCODE_WB), .b(4'b0100), .lt(comparator_12_lt));  // open: gt, eq
  Comparator #(.width(4)) comparator_13 (.a(OPCODE_WB), .b(4'b0110), .eq(JALR));  // open: gt, lt
  Comparator #(.width(4)) comparator_14 (.a(OPCODE_WB), .b(4'b0011), .eq(comparator_14_eq[1]));  // open: gt, lt
  or or_3 (WB, comparator_12_lt, JALR);
  Multiplexer #(.select(2), .width(32), .enable("false")) multiplexer_12 (
    .in0(RESULT_WB), .in1(PC_1_WB), .in2(mem_wb_buffer_1_ram_out_2), .out(WB_Data),
    .sel({comparator_14_eq[1], JALR}));  // open: in3
  Multiplexer #(.width(4), .enable("false")) multiplexer_13 (.in0(Rx_WB), .in1(Ry_WB), .out(REG_WB), .sel(JALR));

  // Notes on the sheet:
  //   contents of rom_1 (hex, n*v repeats v):
  //   2600000a 24400001 54600001 544ffffd 25500001 45000000 55600001 500ffffc 500fffff
  //   BEQ?
  //   jalr?
endmodule

module Dual_Ported_Register_File (
  input  CLK,
  input  WrEN,
  input  [3:0] WrREGNO,
  input  [3:0] RdREGNO1,
  input  [3:0] RdREGNO2,
  input  [31:0] INPUT,
  output [31:0] OUT1,
  output [31:0] OUT2
);

  wire En_a0, En_a1, En_a2, En_a3, En_a4, En_at, En_fp, En_k0, En_ra, En_s0, En_s1, En_s2, En_s3, En_sp,
       En_v0;
  wire [31:0] a0, a1, a2, a3, a4, at, fp, k0, ra, s0, s1, s2, s3, sp, v0, zero;

  Decoder #(.select(4), .disabled(0)) decoder_1 (
    .out1(En_at), .out2(En_v0), .out3(En_a0), .out4(En_a1), .out5(En_a2), .out6(En_a3), .out7(En_a4),
    .out8(En_s0), .out9(En_s1), .out10(En_s2), .out11(En_s3), .out12(En_k0), .out13(En_sp), .out14(En_fp),
    .out15(En_ra), .sel(WrREGNO), .en(WrEN));  // open: out0
  Register #(.width(32)) u_zero (.D(INPUT), .en(1'b0), .Q(zero), .clk(CLK));  // open: clr
  Register #(.width(32)) u_at (.D(INPUT), .en(En_at), .Q(at), .clk(CLK));  // open: clr
  Register #(.width(32)) u_v0 (.D(INPUT), .en(En_v0), .Q(v0), .clk(CLK));  // open: clr
  Register #(.width(32)) u_a0 (.D(INPUT), .en(En_a0), .Q(a0), .clk(CLK));  // open: clr
  Register #(.width(32)) u_a1 (.D(INPUT), .en(En_a1), .Q(a1), .clk(CLK));  // open: clr
  Register #(.width(32)) u_a2 (.D(INPUT), .en(En_a2), .Q(a2), .clk(CLK));  // open: clr
  Register #(.width(32)) u_a3 (.D(INPUT), .en(En_a3), .Q(a3), .clk(CLK));  // open: clr
  Register #(.width(32)) u_a4 (.D(INPUT), .en(En_a4), .Q(a4), .clk(CLK));  // open: clr
  Multiplexer #(.select(4), .width(32), .disabled(0), .enable("false")) multiplexer_1 (
    .in0(zero), .in1(at), .in2(v0), .in3(a0), .in4(a1), .in5(a2), .in6(a3), .in7(a4), .in8(s0), .in9(s1),
    .in10(s2), .in11(s3), .in12(k0), .in13(sp), .in14(fp), .in15(ra), .out(OUT2), .sel(RdREGNO2));
  Register #(.width(32)) u_s0 (.D(INPUT), .en(En_s0), .Q(s0), .clk(CLK));  // open: clr
  Register #(.width(32)) u_s1 (.D(INPUT), .en(En_s1), .Q(s1), .clk(CLK));  // open: clr
  Register #(.width(32)) u_s2 (.D(INPUT), .en(En_s2), .Q(s2), .clk(CLK));  // open: clr
  Register #(.width(32)) u_s3 (.D(INPUT), .en(En_s3), .Q(s3), .clk(CLK));  // open: clr
  Register #(.width(32)) u_k0 (.D(INPUT), .en(En_k0), .Q(k0), .clk(CLK));  // open: clr
  Register #(.width(32)) u_sp (.D(INPUT), .en(En_sp), .Q(sp), .clk(CLK));  // open: clr
  Register #(.width(32)) u_fp (.D(INPUT), .en(En_fp), .Q(fp), .clk(CLK));  // open: clr
  Register #(.width(32)) u_ra (.D(INPUT), .en(En_ra), .Q(ra), .clk(CLK));  // open: clr
  Multiplexer #(.select(4), .width(32), .disabled(0), .enable("false")) multiplexer_2 (
    .in0(zero), .in1(at), .in2(v0), .in3(a0), .in4(a1), .in5(a2), .in6(a3), .in7(a4), .in8(s0), .in9(s1),
    .in10(s2), .in11(s3), .in12(k0), .in13(sp), .in14(fp), .in15(ra), .out(OUT1), .sel(RdREGNO1));

  // Notes on the sheet:
  //   MODIFY AT YOUR OWN RISK
endmodule

// IF/ BUFFER
module IF_IDRR_Buffer (
  input  [31:0] PC_1,
  input  [31:0] Instruction,
  input  Clear,
  input  EN,
  input  Clock,
  output [31:0] PC_1_OUT,
  output [31:0] INST_OUT
);

  Register #(.width(32)) PC (.D(PC_1), .en(EN), .Q(PC_1_OUT), .clk(Clock), .clr(Clear));
  Register #(.width(32)) u_Instruction (.D(Instruction), .en(EN), .Q(INST_OUT), .clk(Clock), .clr(Clear));

  // Other names for the same wires on the sheet: CLK = Clock; CLR = Clear
endmodule

// ID/DR BUFFER
module IDRR_EX_Buffer (
  input  Clear,
  input  EN,
  input  Clock,
  input  [31:0] PC_IN,
  input  [31:0] Offset_IN,
  input  [31:0] Rdata1IN,
  input  [31:0] Rdata2IN,
  input  [3:0] OPCODE_IN,
  input  [3:0] Rx_In,
  input  [3:0] Ry_In,
  output [31:0] PC_OUT,
  output [31:0] Offset_OUT,
  output [31:0] Rdata1OUT,
  output [31:0] Rdata2OUT,
  output [3:0] OPCODE_OUT,
  output [3:0] Rx_IN_2,
  output [3:0] Ry_IN_2
);

  Register #(.width(4)) OPCODE (.D(OPCODE_IN), .en(EN), .Q(OPCODE_OUT), .clk(Clock), .clr(Clear));
  Register #(.width(32)) PC (.D(PC_IN), .en(EN), .Q(PC_OUT), .clk(Clock), .clr(Clear));
  Register #(.width(32)) Offset (.D(Offset_IN), .en(EN), .Q(Offset_OUT), .clk(Clock), .clr(Clear));
  Register #(.width(32)) Rdata1 (.D(Rdata1IN), .en(EN), .Q(Rdata1OUT), .clk(Clock), .clr(Clear));
  Register #(.width(32)) Rdata2 (.D(Rdata2IN), .en(EN), .Q(Rdata2OUT), .clk(Clock), .clr(Clear));
  Register #(.width(4)) Rx (.D(Rx_In), .en(EN), .Q(Rx_IN_2), .clk(Clock), .clr(Clear));
  Register #(.width(4)) Ry (.D(Ry_In), .en(EN), .Q(Ry_IN_2), .clk(Clock), .clr(Clear));

  // Other names for the same wires on the sheet: CLK = Clock; CLR = Clear
endmodule

module EX_MEM_Buffer (
  input  Clear,
  input  EN,
  input  Clock,
  input  [31:0] Offset_IN,
  input  [31:0] Rdata1IN,
  input  [31:0] Rdata2IN,
  input  [31:0] Result_IN,
  input  [3:0] OPCODE_IN,
  input  [3:0] Rx_In,
  input  [3:0] Ry_In,
  input  [31:0] PC_1_IN,
  input  BRANCH,
  input  [31:0] NEWPC,
  output [31:0] Offset_OUT,
  output [31:0] Rdata1_OUT,
  output [31:0] Rdata2_OUT,
  output [31:0] Result_Out,
  output [3:0] OPCODE_OUT,
  output [3:0] Rx_OUT,
  output [3:0] Ry_OUT,
  output [31:0] PC_1_OUT,
  output BRANCH_2,
  output [31:0] NEWPC_2
);

  Register #(.width(32)) Rdata2 (.D(Rdata2IN), .en(EN), .Q(Rdata2_OUT), .clk(Clock), .clr(Clear));
  Register #(.width(32)) RESULT (.D(Result_IN), .en(EN), .Q(Result_Out), .clk(Clock), .clr(Clear));
  Register #(.width(4)) OPCODE (.D(OPCODE_IN), .en(EN), .Q(OPCODE_OUT), .clk(Clock), .clr(Clear));
  Register #(.width(4)) Ry (.D(Ry_In), .en(EN), .Q(Ry_OUT), .clk(Clock), .clr(Clear));
  Register #(.width(32)) PC_1 (.D(PC_1_IN), .en(EN), .Q(PC_1_OUT), .clk(Clock), .clr(Clear));
  Register #(.width(1)) u_BRANCH (.D(BRANCH), .en(EN), .Q(BRANCH_2), .clk(Clock), .clr(Clear));
  Register #(.width(32)) u_NEWPC (.D(NEWPC), .en(EN), .Q(NEWPC_2), .clk(Clock), .clr(Clear));
  Register #(.width(32)) Offset (.D(Offset_IN), .en(EN), .Q(Offset_OUT), .clk(Clock), .clr(Clear));
  Register #(.width(32)) Rdata1 (.D(Rdata1IN), .en(EN), .Q(Rdata1_OUT), .clk(Clock), .clr(Clear));
  Register #(.width(4)) Rx (.D(Rx_In), .en(EN), .Q(Rx_OUT), .clk(Clock), .clr(Clear));

  // Other names for the same wires on the sheet: CLK = Clock; CLR = Clear
endmodule

// MEM/WB BUFFER
module MEM_WB_Buffer (
  input  EN,
  input  Clock,
  input  [31:0] PC_1_IN,
  input  [31:0] Result_IN,
  input  [31:0] RAM_OUT,
  input  [3:0] OPCODE_IN,
  input  [3:0] Rx_In,
  input  [3:0] Ry_In,
  output [31:0] PC_1_OUT,
  output [31:0] Result_Out,
  output [31:0] RAM_OUT_2,
  output [3:0] OPCODE_OUT,
  output [3:0] Rx_OUT,
  output [3:0] Ry_OUT
);

  wire CLR;

  Register #(.width(32)) RESULT (.D(Result_IN), .en(EN), .Q(Result_Out), .clk(Clock));  // open: clr
  Register #(.width(32)) RAM (.D(RAM_OUT), .en(EN), .Q(RAM_OUT_2), .clk(Clock));  // open: clr
  Register #(.width(4)) OPCODE (.D(OPCODE_IN), .en(EN), .Q(OPCODE_OUT), .clk(Clock), .clr(CLR));
  Register #(.width(4)) Ry (.D(Ry_In), .en(EN), .Q(Ry_OUT), .clk(Clock));  // open: clr
  Register #(.width(4)) Rx (.D(Rx_In), .en(EN), .Q(Rx_OUT), .clk(Clock));  // open: clr
  Register #(.width(32)) PC_1 (.D(PC_1_IN), .en(EN), .Q(PC_1_OUT), .clk(Clock));  // open: clr

  // Other names for the same wires on the sheet: CLK = Clock
endmodule

module ALU (
  input  [1:0] FUNC,
  input  [31:0] A,
  input  [31:0] B,
  output [31:0] OUT
);

  wire [31:0] adder_1_out, adder_2_out, nand_1_out, subtractor_1_out;

  Adder #(.width(32)) adder_1 (.a(A), .b(B), .out(adder_1_out), .cin(1'b0));  // open: cout
  assign nand_1_out = ~(A & B);  // NAND_Gate nand_1, 32 bits wide
  Subtractor #(.width(32)) subtractor_1 (.a(A), .b(B), .out(subtractor_1_out), .bin(1'b0));  // open: bout
  Adder #(.width(32)) adder_2 (.a(A), .b({32{1'b0}}), .out(adder_2_out), .cin(1'b1));  // open: cout
  Multiplexer #(.select(2), .width(32), .disabled(0), .enable("false")) multiplexer_1 (
    .in0(adder_1_out), .in1(nand_1_out), .in2(subtractor_1_out), .in3(adder_2_out), .out(OUT), .sel(FUNC));

  // Notes on the sheet:
  //   MODIFY AT YOUR OWN RISK
endmodule

module Forwarding_Unit (
  input  [3:0] EX_Rx,
  input  [3:0] MEM_Rx,
  input  [3:0] WB_Rx,
  input  [31:0] EX_Result,
  input  [31:0] MEM_Result,
  input  [31:0] RAM_Result,
  input  [31:0] WB_Result,
  input  [3:0] WB_OPCODE,
  input  [3:0] EX_OPCODE,
  input  [3:0] MEM_OPCODE,
  input  [31:0] IDDR_Rout1,
  input  [31:0] IDDR_Rout2,
  input  [3:0] IDDR_Rx,
  input  [3:0] IDDR_Ry,
  input  [3:0] IDDR_Rz,
  input  [3:0] IDDR_Opcode,
  output [31:0] out_17,
  output [31:0] out_18
);

  wire _0, _0__Ry, _1, _1__Ry, _2, _2__Ry, _3, _3__Ry, ADD_NAND, comparator_1_lt, comparator_2_eq,
       comparator_12_lt, comparator_13_eq, comparator_17_lt, comparator_18_eq, ENABLE_EX, ENABLE_MEM,
       ENABLE_WB, EX__FRy, EX__FRz, LW, MEM__FRy, MEM__FRz, MEM_FORWARD, Ry_FORWARD_EX_Rx, Ry_FORWARD_MEM_Rx,
       Ry_FORWARD_WB_Rx, Ry_MEM_FORWARD, Rz_FORWARD_EX_Rx, Rz_FORWARD_MEM_Rx, Rz_FORWARD_WB_Rx, WB__FRy,
       WB__FRz;
  wire [1:0] Ry, Rz;
  wire [31:0] MEM_Result_t;

  Comparator #(.width(4)) comparator_1 (.a(EX_OPCODE), .b(4'b0100), .lt(comparator_1_lt));  // open: gt, eq
  Comparator #(.width(4)) comparator_2 (.a(EX_OPCODE), .b(4'b0110), .eq(comparator_2_eq));  // open: gt, lt
  or or_1 (ENABLE_EX, comparator_1_lt, comparator_2_eq);
  Comparator #(.width(4)) comparator_3 (.a(IDDR_Opcode), .b(4'b0010), .lt(ADD_NAND));  // open: gt, eq
  Comparator #(.width(4)) comparator_4 (.a(IDDR_Ry), .b(EX_Rx), .eq(EX__FRy));  // open: gt, lt
  Comparator #(.width(4)) comparator_5 (.a(IDDR_Rz), .b(EX_Rx), .eq(EX__FRz));  // open: gt, lt
  Comparator #(.width(3)) comparator_6 (
    .a({Rz_FORWARD_EX_Rx, Rz_FORWARD_MEM_Rx, Rz_FORWARD_WB_Rx}), .b(3'b000), .eq(_0));  // open: gt, lt
  Comparator #(.width(3)) comparator_7 (
    .a({Rz_FORWARD_EX_Rx, Rz_FORWARD_MEM_Rx, Rz_FORWARD_WB_Rx}), .b(3'b001), .eq(_1));  // open: gt, lt
  Comparator #(.width(3)) comparator_8 (
    .a({Rz_FORWARD_EX_Rx, Rz_FORWARD_MEM_Rx, Rz_FORWARD_WB_Rx}), .b(3'b010), .eq(_2));  // open: gt, lt
  Comparator #(.width(3)) comparator_9 (
    .a({Rz_FORWARD_EX_Rx, Rz_FORWARD_MEM_Rx, Rz_FORWARD_WB_Rx}), .b(3'b011), .eq(_3));  // open: gt, lt
  Comparator #(.width(4)) comparator_10 (.a(IDDR_Ry), .b(MEM_Rx), .eq(MEM__FRy));  // open: gt, lt
  Comparator #(.width(4)) comparator_11 (.a(IDDR_Rz), .b(MEM_Rx), .eq(MEM__FRz));  // open: gt, lt
  or or_2 (MEM_FORWARD, _2, _3);
  Comparator #(.width(4)) comparator_12 (.a(MEM_OPCODE), .b(4'b0100), .lt(comparator_12_lt));  // open: gt, eq
  Comparator #(.width(4)) comparator_13 (.a(MEM_OPCODE), .b(4'b0110), .eq(comparator_13_eq));  // open: gt, lt
  Comparator #(.width(4)) comparator_14 (.a(MEM_OPCODE), .b(4'b0011), .eq(LW));  // open: gt, lt
  Multiplexer #(.select(2), .width(32), .enable("false")) multiplexer_1 (
    .in0(IDDR_Rout1), .in1(EX_Result), .in2(MEM_Result_t), .in3(WB_Result), .out(out_17), .sel(Ry));
  and and_1 (Ry_FORWARD_EX_Rx, ENABLE_EX, EX__FRy);
  and and_2 (Rz_FORWARD_EX_Rx, ENABLE_EX, EX__FRz);
  or or_3 (ENABLE_MEM, comparator_12_lt, comparator_13_eq);
  assign Rz = _0 ? 2'b00 : 2'bz;  // Controlled_Buffer controlled_buffer_1
  assign Rz = Rz_FORWARD_EX_Rx ? 2'b01 : 2'bz;  // Controlled_Buffer controlled_buffer_2
  assign Rz = MEM_FORWARD ? 2'b10 : 2'bz;  // Controlled_Buffer controlled_buffer_3
  assign Rz = _1 ? 2'b11 : 2'bz;  // Controlled_Buffer controlled_buffer_4
  Multiplexer #(.width(32), .enable("false")) multiplexer_2 (
    .in0(MEM_Result), .in1(RAM_Result), .out(MEM_Result_t), .sel(LW));
  Comparator #(.width(4)) comparator_15 (.a(IDDR_Ry), .b(WB_Rx), .eq(WB__FRy));  // open: gt, lt
  Comparator #(.width(4)) comparator_16 (.a(IDDR_Rz), .b(WB_Rx), .eq(WB__FRz));  // open: gt, lt
  Comparator #(.width(4)) comparator_17 (.a(WB_OPCODE), .b(4'b0100), .lt(comparator_17_lt));  // open: gt, eq
  Comparator #(.width(4)) comparator_18 (.a(WB_OPCODE), .b(4'b0110), .eq(comparator_18_eq));  // open: gt, lt
  and and_3 (Ry_FORWARD_MEM_Rx, ENABLE_MEM, MEM__FRy);
  and and_4 (Rz_FORWARD_MEM_Rx, ENABLE_MEM, MEM__FRz);
  or or_4 (ENABLE_WB, comparator_17_lt, comparator_18_eq);
  Multiplexer #(.select(2), .width(32), .enable("false")) multiplexer_3 (
    .in0(IDDR_Rout2), .in1(EX_Result), .in2(MEM_Result_t), .in3(WB_Result), .out(out_18), .sel(Rz));
  and and_5 (Ry_FORWARD_WB_Rx, ENABLE_EX, WB__FRy);
  Comparator #(.width(3)) comparator_19 (
    .a({Ry_FORWARD_EX_Rx, Ry_FORWARD_MEM_Rx, Ry_FORWARD_WB_Rx}), .b(3'b000), .eq(_0__Ry));  // open: gt, lt
  Comparator #(.width(3)) comparator_20 (
    .a({Ry_FORWARD_EX_Rx, Ry_FORWARD_MEM_Rx, Ry_FORWARD_WB_Rx}), .b(3'b001), .eq(_1__Ry));  // open: gt, lt
  Comparator #(.width(3)) comparator_21 (
    .a({Ry_FORWARD_EX_Rx, Ry_FORWARD_MEM_Rx, Ry_FORWARD_WB_Rx}), .b(3'b010), .eq(_2__Ry));  // open: gt, lt
  Comparator #(.width(3)) comparator_22 (
    .a({Ry_FORWARD_EX_Rx, Ry_FORWARD_MEM_Rx, Ry_FORWARD_WB_Rx}), .b(3'b011), .eq(_3__Ry));  // open: gt, lt
  and and_6 (Rz_FORWARD_WB_Rx, ENABLE_EX, WB__FRz);
  or or_5 (Ry_MEM_FORWARD, _2__Ry, _3__Ry);
  assign Ry = _0__Ry ? 2'b00 : 2'bz;  // Controlled_Buffer controlled_buffer_5
  assign Ry = Ry_FORWARD_EX_Rx ? 2'b01 : 2'bz;  // Controlled_Buffer controlled_buffer_6
  assign Ry = Ry_MEM_FORWARD ? 2'b10 : 2'bz;  // Controlled_Buffer controlled_buffer_7
  assign Ry = _1__Ry ? 2'b11 : 2'bz;  // Controlled_Buffer controlled_buffer_8
endmodule
